# Fritzing sketch Costco_controller (saved by Fritzing 0.9.3b)

parts:
  U1 = Voltage Regulator [part_number=78M05 package=to220-igo]
  LED_Strip1 = Molex Picoblade Series Header [package=Picoblade-53398-0571]
  Power_plug1 = Power plug  # not connected
  Q2 = Basic FET N-Channel [part_number=VS3019AD package="TO220 [THT]"]
  Q1 = Basic FET N-Channel [part_number=CMD20P03 package="TO220 [THT]"]
  L5 = Ceramic Capacitor [capacitance="100 nF" package="0805 [SMD, multilayer]"]
  U2 = IC, DIP package, 20 pins [chip_label=IC part_number=STM8S003F3]
  R1 = Resistor [tolerance=±5% resistance=220 package=THT]
  IR1 = TSOP312.., 314.. [package=THT]
  C2 = Electrolytic Capacitor [capacitance=1mF voltage=35V package="100 mil [THT, electrolytic]"]
  R2 = Resistor [tolerance=±5% resistance=15 package=THT]
  R6 = Resistor [tolerance=±5% resistance=47k package=THT]
  R4 = Resistor [tolerance=±5% resistance=1k package=THT]
  R17 = Resistor [tolerance=±5% resistance=10k package=THT]
  C13 = Ceramic Capacitor [capacitance=100nF package="100 mil [THT, multilayer]"]
  C12 = Ceramic Capacitor [capacitance=100nF package="100 mil [THT, multilayer]"]
  C14 = Ceramic Capacitor [capacitance=100nF package="100 mil [THT, multilayer]"]
  Board_Header = Molex Picoblade Series Header [package=Picoblade-53398-0471]
  R16 = Resistor [tolerance=±5% resistance=47k package=THT]
  C2_2 = Ceramic Capacitor [capacitance=100nF package="100 mil [THT, multilayer]"]
  C9 = Ceramic Capacitor [capacitance=100nF package="100 mil [THT, multilayer]"]
  R15 = Resistor [tolerance=±5% resistance=47k package=THT]
  C15 = Electrolytic Capacitor [capacitance=47µF voltage=35V package="100 mil [THT, electrolytic]"]
  C16 = Electrolytic Capacitor [capacitance=47µF voltage=16V package="100 mil [THT, electrolytic]"]

nets:
  GND: U1.GND, C2.-, Board_Header.2
  N1: U1.IN, LED_Strip1.5, C2.+
  N2: LED_Strip1.1, L5.1
  N3: LED_Strip1.2, R1.Pin_1
  N4: LED_Strip1.3, R2.Pin_1
  N5: LED_Strip1.4, Q2.drain
  N6: Q2.gate, R6.Pin_0, R4.Pin_0
  N7: Q2.source, R6.Pin_1, C13.0, C12.0, C14.0
  N8: Q1.drain, L5.0
  N9: Q1.source, C15.+
  N10: U2.pin1, R1.Pin_0
  N11: U2.pin4, R17.Pin_1, C13.1
  N12: U2.pin8, C12.1
  N13: U2.pin9, C14.1
  N14: U2.pin10, IR1.GND, R16.Pin_0
  N15: U2.pin18, Board_Header.3
  N16: R17.Pin_0, Board_Header.4, R16.Pin_1, C16.+
  N17: C2_2.0, C9.0, R15.Pin_0

notes:
  Costco Controller, ESP8266/RGB+W/WS2812 LED Strip controller, 2.0
  LED Strip Connector
  1 - 24V - Black
  2 - DIN - Red
  3 - Check - Green
  4 - W - Yellow
  5 - Gnd - Blue
