# Fritzing sketch ESP 8266 - MCUIOT - BME-GD (saved by Fritzing 0.9.3b)

parts:
  U3 = NodeMCU V1.0
  BME-280 = GY-BMEP280 Barometric Pressure Sensor - Breakout
  ADS1115 = Adafruit ADS1115 16Bit I2C ADC
  Open = smd LED [color="Red (633nm)" package="0603 [SMD]"]
  Closed = LED - 5mm [color="Green (560nm)" package="5 mm [THT]"]

nets:
  3V3: U3.3V3, BME-280.VCC, ADS1115.VDD
  GND: U3.GND, BME-280.GND, ADS1115.GND
  N1: U3.D5, BME-280.SCL, ADS1115.SCL
  N2: U3.D6, BME-280.SDA, ADS1115.SDA
  5V: ADS1115.AIN3, Open.anode, Closed.anode
  N3: ADS1115.AIN1, Open.cathode
  N4: ADS1115.AIN0, Closed.cathode

notes:
  MCUIOT
  BME-GD
  MCUIOT - BME-GD
  Garage Door Monitor

custom parts:
  NodeMCU V1.0: ESP8266 based NodeMCU
  GY-BMEP280 Barometric Pressure Sensor - Breakout: The BME280 is a chip which was originally designed for the next generation of smartphones. It is made up of a very accurate pressure sensor and an associated temperature sensor which helps calibrate the pressure readings. And just for fun they threw in a pretty solid humidity sensor in there as well! So with an I2C connection you have access to enough weather data to make some pretty good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
  Adafruit ADS1115 16Bit I2C ADC: For microcontrollers without an analog-to-digital converter or when you want a higher-precision ADC, the ADS1115 provides 16-bit precision at 860 samples/second over I2C. The chip can be configured as 4 single-ended input channels, or two differential channels. As a nice bonus, it even includes a programmable gain amplifier, up to x16, to help boost up smaller single/differential signals to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
