# Fritzing sketch ESP 8266 - MCUIOT - BME-YL (saved by Fritzing 0.9.3b)

parts:
  U3 = NodeMCU V1.0
  Q1 = NPN-Transistor [part_number=2N3904 package="TO92 [THT]"]
  R1 = Resistor [tolerance=±5% resistance=1k package=THT]
  YL-69 = Soil Moisture Sensor
  BME-280 = GY-BMEP280 Barometric Pressure Sensor - Breakout

nets:
  VCC: U3.3V3, YL-69.VCC, BME-280.VCC
  GND: U3.GND, Q1.E, BME-280.GND
  N1: U3.D5, BME-280.SCL
  N2: U3.D6, BME-280.SDA
  N3: U3.D7, R1.Pin_0
  N4: U3.A0, YL-69.SIG
  N5: Q1.B, R1.Pin_1
  N6: Q1.C, YL-69.GND

notes:
  MCUIOT
  BME-YL
  MCUIOT - BME-YL

custom parts:
  NodeMCU V1.0: ESP8266 based NodeMCU
  GY-BMEP280 Barometric Pressure Sensor - Breakout: The BME280 is a chip which was originally designed for the next generation of smartphones. It is made up of a very accurate pressure sensor and an associated temperature sensor which helps calibrate the pressure readings. And just for fun they threw in a pretty solid humidity sensor in there as well! So with an I2C connection you have access to enough weather data to make some pretty good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
