# Fritzing sketch ESP 8266 - MCUIOT - DHT-YL (saved by Fritzing 0.9.3b)

parts:
  U3 = NodeMCU V1.0
  Q1 = NPN-Transistor [part_number=2N3904 package="TO92 [THT]"]
  R1 = Resistor [tolerance=±5% resistance=1k package=THT]
  YL-69 = Soil Moisture Sensor
  DHT22 = Humidity and Temperature Sensor DHT22

nets:
  N1: U3.D2, DHT22.Data-signal
  VCC: U3.3V3, YL-69.VCC, DHT22.Vcc
  N2: U3.GND, Q1.E, DHT22.GND_2
  N3: U3.D5, R1.Pin_0
  N4: U3.A0, YL-69.SIG
  N5: Q1.B, R1.Pin_1
  N6: Q1.C, YL-69.GND

notes:
  MCUIOT
  DHT-YL
  MCUIOT - DHT-YL

custom parts:
  NodeMCU V1.0: ESP8266 based NodeMCU
  Humidity and Temperature Sensor DHT22: Digital relative humidity & temperature sensor DHT22
