# Fritzing sketch mculed_v3_strip (saved by Fritzing 0.9.3b)
circuit board: 8.46667cm x 5.64444cm
stripboards: 1

parts:
  Power_plug_-_5_VDC = Power plug
  R1 = Resistor [tolerance=±5% resistance=470 package=THT]
  IC1 = 74HCT245 [chip_label=74HCT245 package="DIP (Dual Inline) [THT]"]
  U1 = NodeMCU V3.0
  Led_Strip_1 = female pin header, 3 pins [form="♀ (female)"]
  Led_Strip_2 = female pin header, 3 pins [form="♀ (female)"]
  R2 = Resistor [tolerance=±5% resistance=470 package=THT]
  C1 = Electrolytic Capacitor [capacitance=1mF voltage=35V package="200 mil [THT, electrolytic]"]

nets:
  GND: Power_plug_-_5_VDC.GND, IC1.pin10, IC1.pin19, U1.GND#6, U1.GND#13, U1.GND#16, U1.GND#33, Led_Strip_1.pin3, Led_Strip_2.pin3, C1.-
  VCC: Power_plug_-_5_VDC.VCC, IC1.Direction, IC1.pin20, U1.Vin, Led_Strip_1.pin1, Led_Strip_2.pin1, C1.+
  N1: R1.Pin_0, IC1.pin18
  N2: R1.Pin_1, Led_Strip_1.pin2
  N3: IC1.A1, U1.D4
  N4: IC1.pin3, U1.TX
  N5: IC1.pin17, R2.Pin_0
  N6: Led_Strip_2.pin2, R2.Pin_1

notes:
  homebridge-mculed - 5 Volt Strips, ESP8266/RGB/WS2811 LED Strip controller, 3.0
  LED Strip Connector
  1 - 5V - Red
  2 - DIN - Green
  3 - Gnd - White

custom parts:
  74HCT245: A DIP stand-in part for whatever IC you want. With 20 pins on a 300mil dual inline package (DIP) footprint.
  NodeMCU V3.0: ESP8266 based NodeMCU
